# Fritzing sketch Ultimate Alarm Clock - for PCB3 (saved by Fritzing 0.8.7b)
circuit board: 4.18737cm x 5.43543cm
breadboards: 1

parts:
  speaker = Piezo Speaker
  R1 = Resistor [tolerance=±5% resistance=170 package=THT]
  GPS = mystery part, 4 pins [chip_label=GPS]
  LCD = mystery part, 5 pins [chip_label=7segment]
  mega_D22_-_D53 = mystery part, 36 pins [chip_label="mega 22-53"]
  mega_D18-D21 = mystery part, 4 pins [chip_label=mega18-21]
  R6 = Resistor [tolerance=±5% resistance=10k package=THT]
  D_PWM = female pin header, 1 pin [form="♀ (female)"]
  photocell = female pin header, 2 pins [form="♀ (female)"]
  AM/PM = female pin header, 2 pins [form="♀ (female)"]
  alarm_on = female pin header, 2 pins [form="♀ (female)"]
  snooze = female pin header, 2 pins [form="♀ (female)"]
  mega_A8-A10 = mystery part, 3 pins [chip_label=megaA8-A15]
  set_hour = mystery part, 12 pins [chip_label="12 pos switch"]
  set_min = mystery part, 8 pins [chip_label="6 pos switch"]
  LCDmax = mystery part, 3 pins [chip_label=?]
  LCDmin = mystery part, 3 pins [chip_label=?]
  volume = mystery part, 3 pins [chip_label=?]

nets:
  N1: speaker.pin1, R1.Pin_1
  N2: speaker.pin2, GPS.pin4, LCD.pin3, mega_D22_-_D53.pin18, mega_D22_-_D53.pin19, R6.Pin_0, AM/PM.pin2, alarm_on.pin2, snooze.pin2, set_min.pin1, LCDmax.pin3, LCDmin.pin3, volume.pin3
  N3: R1.Pin_0, volume.pin2
  N4: GPS.pin1, LCD.pin4, mega_D22_-_D53.pin1, mega_D22_-_D53.pin36, photocell.pin1, LCDmax.pin1, LCDmin.pin1
  N5: GPS.pin2, mega_D18-D21.pin1
  N6: GPS.pin3, mega_D18-D21.pin2
  N7: LCD.pin1, mega_D18-D21.pin4
  N8: LCD.pin2, mega_D18-D21.pin3
  N9: mega_D22_-_D53.pin2, set_hour.pin3
  N10: mega_D22_-_D53.pin3, set_hour.pin2
  N11: mega_D22_-_D53.pin4, set_hour.pin1
  N12: mega_D22_-_D53.pin5, set_hour.pin12
  N13: mega_D22_-_D53.pin6, set_hour.pin11
  N14: mega_D22_-_D53.pin7, set_hour.pin10
  N15: mega_D22_-_D53.pin8, set_hour.pin9
  N16: mega_D22_-_D53.pin9, set_hour.pin8
  N17: mega_D22_-_D53.pin10, set_hour.pin7
  N18: mega_D22_-_D53.pin11, set_hour.pin5
  N19: mega_D22_-_D53.pin12, set_min.pin8
  N20: mega_D22_-_D53.pin13, set_min.pin7
  N21: mega_D22_-_D53.pin14, set_min.pin6
  N22: mega_D22_-_D53.pin15, set_min.pin5
  N23: mega_D22_-_D53.pin16, set_min.pin3
  N24: mega_D22_-_D53.pin17, set_min.pin4
  N25: mega_D22_-_D53.pin20, set_hour.pin6
  N26: mega_D22_-_D53.pin22, AM/PM.pin1
  N27: mega_D22_-_D53.pin25, snooze.pin1
  N28: mega_D22_-_D53.pin30, alarm_on.pin1
  N29: mega_D22_-_D53.pin35, set_hour.pin4
  N30: R6.Pin_1, photocell.pin2, mega_A8-A10.pin1
  N31: D_PWM.pin1, volume.pin1
  N32: mega_A8-A10.pin2, LCDmin.pin2
  N33: mega_A8-A10.pin3, LCDmax.pin2

notes:
  RKH
  2014
  Clock
