# Fritzing sketch Ultimate Alarm Clock - mega (saved by Fritzing 0.8.7b)
breadboards: 1

parts:
  display = 7-Segment LED I2C Backpack (red)
  snooze = Square Pushbutton
  alarm_on = Square Pushbutton
  LCD_max = POT [package=pot_alpha_rv16af-20]
  LCD_min = POT [package=pot_alpha_rv16af-20]
  alarm_volume = POT [package=pot_alpha_rv16af-20]
  speaker = Piezo Speaker
  AM/PM = Square Pushbutton
  GPS = mystery part, 4 pins [chip_label=GPS]
  time_zone = mystery part, 6 pins [chip_label="5 pos switch"]
  Microcontroller = Arduino Mega 2560 (Rev3)
  set_hour = mystery part, 13 pins [chip_label="12 pos switch"]
  set_min = mystery part, 7 pins [chip_label="6 pos switch"]
  R1 = Resistor [tolerance=±5% resistance=170 package=THT]
  photocell = Photocell (LDR) [package=THT]
  R3 = Resistor [tolerance=±5% resistance=10k package=THT]

nets:
  N1: display.V+, LCD_max.E, LCD_min.E, GPS.pin3, Microcontroller.IOREF, photocell.pin_1
  GND: display.GND, snooze.leg1, alarm_on.leg1, LCD_max.A, LCD_min.A, alarm_volume.E, speaker.pin2, AM/PM.leg1, GPS.pin4, time_zone.pin6, Microcontroller.GND, set_hour.pin13, set_min.pin7, R3.Pin_0
  N2: display.SDA, Microcontroller.D20/SDA, Microcontroller.SDA
  N3: display.SCL, Microcontroller.D21/SCL, Microcontroller.SCL
  N4: snooze.leg0, Microcontroller.D3_PWM
  N5: alarm_on.leg0, Microcontroller.D5_PWM
  N6: LCD_max.S, Microcontroller.A1
  N7: LCD_min.S, Microcontroller.A0
  N8: alarm_volume.A, Microcontroller.D13_PWM
  N9: alarm_volume.S, R1.Pin_0
  N10: speaker.pin1, R1.Pin_1
  N11: AM/PM.leg0, Microcontroller.D6_PWM
  N12: GPS.pin1, Microcontroller.D2_PWM
  N13: GPS.pin2, Microcontroller.D4_PWM
  N14: time_zone.pin1, Microcontroller.D8_PWM
  N15: time_zone.pin2, Microcontroller.D9_PWM
  N16: time_zone.pin3, Microcontroller.D10_PWM
  N17: time_zone.pin4, Microcontroller.D11_PWM
  N18: time_zone.pin5, Microcontroller.D12_PWM
  N19: Microcontroller.A2, photocell.pin_0, R3.Pin_1
  N20: Microcontroller.D22, set_hour.pin1
  N21: Microcontroller.D23, set_hour.pin2
  N22: Microcontroller.D24, set_hour.pin3
  N23: Microcontroller.D25, set_hour.pin4
  N24: Microcontroller.D26, set_hour.pin5
  N25: Microcontroller.D27, set_hour.pin6
  N26: Microcontroller.D28, set_hour.pin7
  N27: Microcontroller.D29, set_hour.pin8
  N28: Microcontroller.D30, set_hour.pin9
  N29: Microcontroller.D31, set_hour.pin10
  N30: Microcontroller.D32, set_hour.pin11
  N31: Microcontroller.D33, set_hour.pin12
  N32: Microcontroller.D38, set_min.pin1
  N33: Microcontroller.D39, set_min.pin2
  N34: Microcontroller.D40, set_min.pin3
  N35: Microcontroller.D41, set_min.pin4
  N36: Microcontroller.D42, set_min.pin5
  N37: Microcontroller.D43, set_min.pin6

custom parts:
  7-Segment LED I2C Backpack (red): 4-digit, 7-segment LED Display with I2C Control
